# Fritzing sketch NightLight (saved by Fritzing 0.9.5d)
breadboards: 1

parts:
  Part1 = Arduino Leonardo (Rev3b)
  LED1 = RGB LED (com. cathode, rgb) [package="5 mm [THT]"]
  R1 = Resistor [tolerance=±5% resistance=220 package=THT]
  R2 = Resistor [tolerance=±5% resistance=220 package=THT]
  R3 = Resistor [tolerance=±5% resistance=220 package=THT]
  Part2 = Breakout Board for Electret Microphone
  S1 = Pushbutton [package="[THT]"]
  R4 = PHOTOCELL [package=photocell]
  R5 = Resistor [tolerance=±5% resistance=220 package="2512 [SMD]"]
  R6 = Resistor [tolerance=±5% resistance=0 package="0402 [SMD]"]
  R7 = Resistor [tolerance=±5% resistance=220 package="2512 [SMD]"]

nets (from the breadboard view):
  N1: Part1.D2/SDA, S1.Pin_3
  N2: Part1.D3_PWM/SCL, R1.Pin_0
  N3: Part1.D5_PWM, R2.Pin_0
  N4: Part1.D6_PWM/A7, R3.Pin_0
  5V: Part1.5V, Part2.VCC, R4.P$1, R6.Pin_0
  GND: Part1.GND, LED1.green_anode, Part2.GND, S1.Pin_1, S1.Pin_2, R5.Pin_1, R7.Pin_1
  N5: Part1.A0, R4.P$2, R5.Pin_0
  N6: Part1.A1, R6.Pin_1, R7.Pin_0
  N7: Part1.A2, Part2.AUD
  N8: LED1.red_anode, R1.Pin_1
  N9: LED1.common_cathode, R2.Pin_1
  N10: LED1.blue_anode, R3.Pin_1
